# Fritzing sketch cabling (saved by Fritzing 0.9.3b)
breadboards: 1

parts:
  Composant1 = Arduino Nano (Rev3.0)
  J1 = Basic Servo
  J2 = Basic Servo
  Composant2 = Thumb Joystick

nets:
  GND: Composant1.GND, J1.gnd, J2.gnd, Composant2.GND
  N1: Composant1.D9, J1.pulse
  N2: Composant1.D10, J2.pulse
  VCC: Composant1.5V, J1.vcc, J2.vcc, Composant2.VCC
  N3: Composant1.A1, Composant2.HORZ
  N4: Composant1.A0, Composant2.VERT
